# Fritzing sketch unkrautroboter (saved by Fritzing 1.0.5)

parts:
  XL4015 = RioRand LM2596  # not connected
  D1 = SOLAR-IXYS [package=solarbit-12x1]
  LED1 = RGB LED (com. cathode, rbg) [color="Red (633nm)" current=0.030A package="5 mm [THT]"]
  XL4015_2 = RioRand LM2596
  Bauteil2 = Arduino Pro Mini (5V)
  Mod1 = KY-019 5V Relay Module [package="Breakout board"]
  U2 = LIPO-2000mAh [package=lipo-2000]
  Bauteil3 = Arduino Mega 2560 (Rev3)
  Mod2 = Raspberry Pi 4B
  RY1 = HFD2-012-M-L2 Latching relay [part_number=HFD2-012-M-L2 package="DIP (Dual Inline) [THT]"]
  Bauteil4 = INA 260
  Grove1 = Grove OLED 128x96
  U3 = SWITCH_SPDT [package=kps-1290]
  S1 = Pushbutton [package="[THT]"]

nets:
  N1: D1.A, Mod1.Common
  N2: LED1.red_anode, Bauteil2.SCK
  N3: LED1.blue_anode, Bauteil2.MOSI
  N4: LED1.green_anode, Bauteil2.D10
  N5: XL4015_2.Pin_1, RY1.pin8
  N6: Bauteil2.A4, Bauteil3.D20/SDA, Bauteil3.SDA, Bauteil4.SDA, Grove1.SDA
  N7: Bauteil2.A5, Bauteil3.D21/SCL, Bauteil3.SCL, Bauteil4.SCL, Grove1.SCL
  N8: Bauteil2.D7, Mod1.S
  N9: Bauteil2.D6, RY1.pin2
  N10: Bauteil2.D5, RY1.pin1
  N11: U2.+, U3.P
  N12: Bauteil3.D19/RX1, Mod2.GPIO15
  N13: Bauteil3.D18/TX1, Mod2.GPIO14
  N14: RY1.pin9, Grove1.VCC, S1.Pin_1, S1.Pin_2
  N15: RY1.pin13, S1.Pin_3, S1.Pin_4
  N16: Bauteil4.IN+, U3.S

notes:
  12V
  ==> 5V
  5V
  ==> Überwachung 5V
  Überwachung 5V

custom parts:
  KY-019 5V Relay Module: KY-019 5V Relay module, used to control AC circuits. (Special thanks to vanepp for fixing the PCB holes and other errors)
  HFD2-012-M-L2 Latching relay: Dual coil dpdt latching relay.
  INA 260: Rev. B, add copy
